// Logisim project Contador hasta 7 FFD.circ as structural Verilog: 1 circuit, main circuit Contador
module Contador (
  input  r,
  input  in_2,
  input  in_3,
  input  e,
  input  in_5,
  input  in_6,
  input  in_7,
  input  in_8,
  input  in_9,
  input  in_10,
  input  in_11,
  output [2:0] out_12
);

  wire A_qn, and_1_out, and_2_out, and_3_out, and_4_out, and_5_out, and_6_out, and_7_out, and_8_out,
       and_9_out, B_qn, C_qn, CLK_out, not_1_out, not_2_out, not_3_out, not_4_out, not_5_out, not_6_out,
       not_7_out, not_8_out, not_9_out, not_10_out, not_11_out, not_12_out, not_13_out, not_14_out,
       not_15_out, or_1_out, or_2_out, or_3_out;

  not not_1 (not_1_out, r);
  not not_2 (not_2_out, out_12[1]);
  not not_3 (not_3_out, r);
  not not_4 (not_4_out, out_12[0]);
  not not_5 (not_5_out, r);
  not not_6 (not_6_out, r);
  not not_7 (not_7_out, e);
  not not_8 (not_8_out, r);
  not not_9 (not_9_out, out_12[0]);
  not not_10 (not_10_out, r);
  not not_11 (not_11_out, r);
  not not_12 (not_12_out, e);
  not not_13 (not_13_out, r);
  not not_14 (not_14_out, r);
  not not_15 (not_15_out, e);
  Clock CLK (.out(CLK_out));
  and and_1 (and_1_out, A_qn, out_12[1], out_12[0], not_1_out, e);
  and and_2 (and_2_out, out_12[2], not_2_out, not_3_out);
  and and_3 (and_3_out, out_12[2], not_4_out, not_5_out);
  and and_4 (and_4_out, out_12[2], not_6_out, not_7_out);
  and and_5 (and_5_out, B_qn, out_12[0], not_8_out, e);
  and and_6 (and_6_out, out_12[1], not_9_out, not_10_out);
  and and_7 (and_7_out, out_12[1], not_11_out, not_12_out);
  and and_8 (and_8_out, C_qn, not_13_out, e);
  and and_9 (and_9_out, out_12[0], not_14_out, not_15_out);
  or or_1 (or_1_out, and_1_out, and_2_out, and_3_out, and_4_out);
  or or_2 (or_2_out, and_5_out, and_6_out, and_7_out);
  or or_3 (or_3_out, and_8_out, and_9_out);
  D_Flip_Flop C (.clk(CLK_out), .D(or_3_out), .Q(out_12[0]), .Qn(C_qn), .preset(in_9), .en(in_10), .reset(in_11));
  D_Flip_Flop A (.clk(CLK_out), .D(or_1_out), .Q(out_12[2]), .Qn(A_qn), .preset(in_2), .en(in_3), .reset(in_5));
  D_Flip_Flop B (.clk(CLK_out), .D(or_2_out), .Q(out_12[1]), .Qn(B_qn), .preset(in_6), .en(in_7), .reset(in_8));
endmodule
